# Fritzing sketch ESP8266_and_SI7021 (saved by Fritzing 0.9.3b)
breadboards: 1

parts:
  R1 = Resistor [tolerance=±5% resistance=220 package=THT]
  Adafruit_HUZZAH_ESP8266_Breakout1 = Adafruit HUZZAH ESP8266 Breakout [part_number=2471]
  S1 = Pushbutton [package="[THT]"]
  R2 = Resistor [tolerance=±5% resistance=220 package=THT]
  R3 = Resistor [tolerance=±5% resistance=220 package=THT]
  Part1 = SparkFun_Si7021_Breakout
  LED1 = LED - 5mm [color="Red (633nm)" package="5 mm [THT]"]

nets:
  N1: R1.Pin_0, LED1.anode
  N2: Adafruit_HUZZAH_ESP8266_Breakout1.V+#3, R2.Pin_0, Part1.3.3V
  N3: Adafruit_HUZZAH_ESP8266_Breakout1.#14, S1.Pin_1, S1.Pin_2, R2.Pin_1
  N4: Adafruit_HUZZAH_ESP8266_Breakout1.#5, Part1.SCL
  N5: S1.Pin_3, S1.Pin_4, R3.Pin_1
  N6: R3.Pin_0, Part1.GND
